// Logisim project sequencing.circ as structural Verilog
module main (
  input  in_1,
  input  in_2,
  input  in_3,
  input  in_4,
  input  in_5,
  input  in_6,
  input  in_7,
  input  in_8,
  input  D_E,
  output out_10,
  output out_11,
  output out_12
);

  wire adder_4_1_c4, clock_1_out, clock_2_out, decoder_4to16_1_y0, decoder_4to16_1_y1, decoder_4to16_1_y2,
       decoder_4to16_1_y3, decoder_4to16_1_y4, decoder_4to16_1_y5, decoder_4to16_1_y6, decoder_4to16_1_y7,
       decoder_4to16_1_y8, decoder_4to16_1_y9, decoder_4to16_1_y10, decoder_4to16_1_y11, decoder_4to16_1_y12,
       decoder_4to16_1_y13, decoder_4to16_1_y14, decoder_4to16_1_y15, not_1_out, or_1_out, or_2_out,
       or_3_out, or_4_out, or_5_out, or_6_out, or_7_out, undriven;
  wire [3:0] adder_4_1_s0, multiplexer_1_out, register_4_1_q3;

  Clock clock_1 (.out(clock_1_out));
  not not_1 (not_1_out, out_12);
  D_Latch d_latch_1 (.rst(in_1), .D(in_2), .WE(in_3), .Q(out_10), .NQ(out_11));
  D_Flip_Flop d_flip_flop_1 (.D(not_1_out), .EN(in_5), .rst(in_6), .clk(clock_1_out), .Q(out_12));
  Clock clock_2 (.out(clock_2_out));
  Multiplexer #(.width(4)) multiplexer_1 (
    .in0(adder_4_1_s0), .in1(4'b0000), .out(multiplexer_1_out), .sel(adder_4_1_c4));
  register_4 register_4_1 (
    .rst(in_7), .EN(in_8), .clk(clock_2_out), .D0(multiplexer_1_out[0]), .D1(multiplexer_1_out[1]),
    .D2(multiplexer_1_out[2]), .D3(multiplexer_1_out[3]), .Q0(register_4_1_q3[3]), .Q1(register_4_1_q3[2]),
    .Q2(register_4_1_q3[1]), .Q3(register_4_1_q3[0]));
  adder_4 adder_4_1 (
    .B3(register_4_1_q3[0]), .B2(register_4_1_q3[1]), .B1(register_4_1_q3[2]), .B0(register_4_1_q3[3]),
    .A3(1'b0), .A2(1'b0), .A1(1'b0), .A0(1'b1), .S3(adder_4_1_s0[3]), .S2(adder_4_1_s0[2]),
    .S1(adder_4_1_s0[1]), .S0(adder_4_1_s0[0]), .C4(adder_4_1_c4));  // open: C0
  decoder_4to16 decoder_4to16_1 (
    .A0(adder_4_1_s0[0]), .A1(adder_4_1_s0[1]), .A2(adder_4_1_s0[2]), .A3(adder_4_1_s0[3]), .EN(D_E),
    .Y0(decoder_4to16_1_y0), .Y1(decoder_4to16_1_y1), .Y2(decoder_4to16_1_y2), .Y3(decoder_4to16_1_y3),
    .Y4(decoder_4to16_1_y4), .Y5(decoder_4to16_1_y5), .Y6(decoder_4to16_1_y6), .Y7(decoder_4to16_1_y7),
    .Y8(decoder_4to16_1_y8), .Y9(decoder_4to16_1_y9), .Y10(decoder_4to16_1_y10), .Y11(decoder_4to16_1_y11),
    .Y12(decoder_4to16_1_y12), .Y13(decoder_4to16_1_y13), .Y14(decoder_4to16_1_y14), .Y15(decoder_4to16_1_y15));
  or or_1 (or_1_out, decoder_4to16_1_y2, decoder_4to16_1_y3, decoder_4to16_1_y4, decoder_4to16_1_y5, decoder_4to16_1_y6, decoder_4to16_1_y8, decoder_4to16_1_y10, decoder_4to16_1_y11, decoder_4to16_1_y9, decoder_4to16_1_y13, decoder_4to16_1_y14, decoder_4to16_1_y15);
  or or_2 (or_2_out, decoder_4to16_1_y0, decoder_4to16_1_y1, decoder_4to16_1_y4, decoder_4to16_1_y5, decoder_4to16_1_y6, decoder_4to16_1_y8, decoder_4to16_1_y10, decoder_4to16_1_y11, decoder_4to16_1_y12, decoder_4to16_1_y9, decoder_4to16_1_y14, decoder_4to16_1_y15);
  _7_Segment_Display u_7_segment_display_1 (
    .g(or_1_out), .f(or_2_out), .a(or_3_out), .b(or_4_out), .e(or_5_out), .d(or_6_out), .c(or_7_out),
    .dp(undriven));
  or or_3 (or_3_out, decoder_4to16_1_y0, decoder_4to16_1_y2, decoder_4to16_1_y3, decoder_4to16_1_y5, decoder_4to16_1_y6, decoder_4to16_1_y7, decoder_4to16_1_y9, decoder_4to16_1_y10, decoder_4to16_1_y12, decoder_4to16_1_y8, decoder_4to16_1_y14, decoder_4to16_1_y15);
  or or_4 (or_4_out, decoder_4to16_1_y3, decoder_4to16_1_y4, decoder_4to16_1_y7, decoder_4to16_1_y8, decoder_4to16_1_y2, decoder_4to16_1_y9, decoder_4to16_1_y10, decoder_4to16_1_y0, decoder_4to16_1_y13);
  or or_5 (or_5_out, decoder_4to16_1_y1, decoder_4to16_1_y2, decoder_4to16_1_y10, decoder_4to16_1_y6, decoder_4to16_1_y8, decoder_4to16_1_y11, decoder_4to16_1_y12, decoder_4to16_1_y13, decoder_4to16_1_y14, decoder_4to16_1_y15, decoder_4to16_1_y0);
  or or_6 (or_6_out, decoder_4to16_1_y2, decoder_4to16_1_y3, decoder_4to16_1_y5, decoder_4to16_1_y6, decoder_4to16_1_y8, decoder_4to16_1_y9, decoder_4to16_1_y11, decoder_4to16_1_y12, decoder_4to16_1_y13, decoder_4to16_1_y14, decoder_4to16_1_y0);
  or or_7 (or_7_out, decoder_4to16_1_y3, decoder_4to16_1_y4, decoder_4to16_1_y5, decoder_4to16_1_y6, decoder_4to16_1_y7, decoder_4to16_1_y0, decoder_4to16_1_y9, decoder_4to16_1_y10, decoder_4to16_1_y11, decoder_4to16_1_y8, decoder_4to16_1_y13);
endmodule

module SR_Latch (
  input  R,
  input  S,
  output Q,
  output NQ
);

  nor nor_1 (Q, R, NQ);
  nor nor_2 (NQ, Q, S);
endmodule

module D_Latch (
  input  rst,
  input  D,
  input  WE,
  output Q,
  output NQ
);

  wire and_1_out, and_2_out, and_3_out, not_1_out, not_2_out, or_1_out;

  not not_1 (not_1_out, D);
  and and_1 (and_1_out, not_1_out, WE);
  and and_2 (and_2_out, WE, D);
  not not_2 (not_2_out, rst);
  or or_1 (or_1_out, rst, and_1_out);
  and and_3 (and_3_out, and_2_out, not_2_out);
  SR_Latch sr_latch_1 (.R(or_1_out), .S(and_3_out), .Q(Q), .NQ(NQ));
endmodule

module D_Flip_Flop (
  input  D,
  input  EN,
  input  rst,
  input  clk,
  output Q
);

  wire d_latch_1_q, multiplexer_1_out, not_1_out;

  not not_1 (not_1_out, clk);
  Multiplexer multiplexer_1 (.in0(Q), .in1(D), .out(multiplexer_1_out), .sel(EN));
  D_Latch d_latch_1 (.rst(rst), .D(multiplexer_1_out), .WE(not_1_out), .Q(d_latch_1_q));  // open: NQ
  D_Latch d_latch_2 (.rst(rst), .D(d_latch_1_q), .WE(clk), .Q(Q));  // open: NQ
endmodule

module register_4 (
  input  rst,
  input  EN,
  input  clk,
  input  D0,
  input  D1,
  input  D2,
  input  D3,
  output Q0,
  output Q1,
  output Q2,
  output Q3
);

  D_Flip_Flop d_flip_flop_1 (.D(D0), .EN(EN), .rst(rst), .clk(clk), .Q(Q0));
  D_Flip_Flop d_flip_flop_2 (.D(D1), .EN(EN), .rst(rst), .clk(clk), .Q(Q1));
  D_Flip_Flop d_flip_flop_3 (.D(D2), .EN(EN), .rst(rst), .clk(clk), .Q(Q2));
  D_Flip_Flop d_flip_flop_4 (.D(D3), .EN(EN), .rst(rst), .clk(clk), .Q(Q3));
endmodule

module decoder_4to16 (
  input  A0,
  input  A1,
  input  A2,
  input  A3,
  input  EN,
  output Y0,
  output Y1,
  output Y2,
  output Y3,
  output Y4,
  output Y5,
  output Y6,
  output Y7,
  output Y8,
  output Y9,
  output Y10,
  output Y11,
  output Y12,
  output Y13,
  output Y14,
  output Y15
);

  wire and_1_out, and_2_out, not_1_out;

  not not_1 (not_1_out, A3);
  and and_1 (and_1_out, not_1_out, EN);
  and and_2 (and_2_out, EN, A3);
  decoder_3to8 decoder_3to8_1 (
    .A0(A0), .A1(A1), .A2(A2), .EN(and_1_out), .out_5(Y0), .out_6(Y1), .out_7(Y2), .out_8(Y3), .out_9(Y4),
    .out_10(Y5), .out_11(Y6), .out_12(Y7));
  decoder_3to8 decoder_3to8_2 (
    .A0(A0), .A1(A1), .A2(A2), .EN(and_2_out), .out_5(Y8), .out_6(Y9), .out_7(Y10), .out_8(Y11), .out_9(Y12),
    .out_10(Y13), .out_11(Y14), .out_12(Y15));
endmodule

module decoder_2to4 (
  input  A0,
  input  A1,
  input  EN,
  output Y0,
  output Y1,
  output Y2,
  output Y3
);

  wire not_1_out, not_2_out;

  not not_1 (not_1_out, A0);
  not not_2 (not_2_out, A1);
  and and_1 (Y0, not_1_out, EN, not_2_out);
  and and_2 (Y1, A0, EN, not_2_out);
  and and_3 (Y2, not_1_out, EN, A1);
  and and_4 (Y3, A0, EN, A1);
endmodule

module decoder_3to8 (
  input  A0,
  input  A1,
  input  A2,
  input  EN,
  output out_5,
  output out_6,
  output out_7,
  output out_8,
  output out_9,
  output out_10,
  output out_11,
  output out_12
);

  wire and_1_out, and_2_out, not_1_out;

  not not_1 (not_1_out, A2);
  and and_1 (and_1_out, not_1_out, EN);
  and and_2 (and_2_out, EN, A2);
  // Probe on out_5
  decoder_2to4 decoder_2to4_1 (.A0(A0), .A1(A1), .EN(and_1_out), .Y0(out_5), .Y1(out_6), .Y2(out_7), .Y3(out_8));
  decoder_2to4 decoder_2to4_2 (.A0(A0), .A1(A1), .EN(and_2_out), .Y0(out_9), .Y1(out_10), .Y2(out_11), .Y3(out_12));
endmodule

module encoder_4to2 (
  input  D3,
  input  D2,
  input  D1,
  input  D0,
  output Y0,
  output Y1,
  output V
);

  wire and_1_out, not_1_out;

  not not_1 (not_1_out, D2);
  and and_1 (and_1_out, not_1_out, D1);
  or or_1 (Y1, D2, D3);
  or or_2 (Y0, D3, and_1_out);
  or or_3 (V, Y1, D1, D0);
endmodule

module encoder_8to3 (
  input  in_1,
  input  in_2
);

  encoder_4to2 encoder_4to2_1 ();  // open: D3, D2, D1, D0, Y0, Y1, V
  encoder_4to2 encoder_4to2_2 ();  // open: D3, D2, D1, D0, Y0, Y1, V
endmodule

module mux_2to1 (
  input  D0,
  input  D1,
  input  S,
  input  EN,
  output Y
);

  wire and_1_out, and_2_out, decoder_1to2_1_y0, decoder_1to2_1_y1;

  decoder_1to2 decoder_1to2_1 (.A0(S), .EN(EN), .Y0(decoder_1to2_1_y0), .Y1(decoder_1to2_1_y1));
  and and_1 (and_1_out, D0, decoder_1to2_1_y0);
  and and_2 (and_2_out, decoder_1to2_1_y1, D1);
  or or_1 (Y, and_1_out, and_2_out);
endmodule

module decoder_1to2 (
  input  A0,
  input  EN,
  output Y0,
  output Y1
);

  wire not_1_out;

  not not_1 (not_1_out, A0);
  and and_1 (Y0, not_1_out, EN);
  and and_2 (Y1, A0, EN);
endmodule

module mux_4to1 (
  input  D0,
  input  D1,
  input  D2,
  input  D3,
  input  S1,
  input  S0,
  input  EN,
  output Y
);

  wire mux_2to1_1_y, mux_2to1_2_y;

  mux_2to1 mux_2to1_1 (.D0(D0), .D1(D1), .S(S0), .EN(EN), .Y(mux_2to1_1_y));
  mux_2to1 mux_2to1_2 (.D0(D2), .D1(D3), .S(S0), .EN(EN), .Y(mux_2to1_2_y));
  mux_2to1 mux_2to1_3 (.D0(mux_2to1_1_y), .D1(mux_2to1_2_y), .S(S1), .EN(EN), .Y(Y));
endmodule

module comparer_4 (
  input  A0,
  input  A1,
  input  A2,
  input  A3,
  input  B0,
  input  B1,
  input  B2,
  input  B3,
  input  EN,
  output Y
);

  wire xnor_1_out, xnor_2_out, xnor_3_out, xnor_4_out;

  xnor xnor_1 (xnor_1_out, A0, B0);
  xnor xnor_2 (xnor_2_out, A1, B1);
  xnor xnor_3 (xnor_3_out, A2, B2);
  xnor xnor_4 (xnor_4_out, A3, B3);
  and and_1 (Y, xnor_1_out, xnor_2_out, EN, xnor_3_out, xnor_4_out);
endmodule

module half_adder_1 (
  input  A,
  input  B,
  output C,
  output S
);

  and and_1 (C, A, B);
  xor xor_1 (S, A, B);
endmodule

module full_adder_1 (
  input  A,
  input  B,
  input  Cin,
  output S,
  output Cout
);

  wire and_1_out, and_2_out, or_1_out, xor_1_out;

  xor xor_1 (xor_1_out, A, B);
  and and_1 (and_1_out, A, B);
  or or_1 (or_1_out, A, B);
  and and_2 (and_2_out, or_1_out, Cin);
  xor xor_2 (S, xor_1_out, Cin);
  or or_2 (Cout, and_1_out, and_2_out);
endmodule

module adder_4 (
  input  C0,
  input  B3,
  input  B2,
  input  B1,
  input  B0,
  input  A3,
  input  A2,
  input  A1,
  input  A0,
  output S3,
  output S2,
  output S1,
  output S0,
  output C4
);

  wire full_adder_1_2_cout, full_adder_1_3_cout, full_adder_1_4_cout;

  full_adder_1 full_adder_1_1 (.A(A3), .B(B3), .Cin(full_adder_1_2_cout), .S(S3), .Cout(C4));
  full_adder_1 full_adder_1_2 (.A(A2), .B(B2), .Cin(full_adder_1_3_cout), .S(S2), .Cout(full_adder_1_2_cout));
  full_adder_1 full_adder_1_3 (.A(A1), .B(B1), .Cin(full_adder_1_4_cout), .S(S1), .Cout(full_adder_1_3_cout));
  full_adder_1 full_adder_1_4 (.A(A0), .B(B0), .Cin(C0), .S(S0), .Cout(full_adder_1_4_cout));
endmodule

module subtractor_4 (
  input  Bin,
  input  B3,
  input  B2,
  input  B1,
  input  B0,
  input  A3,
  input  A2,
  input  A1,
  input  A0,
  output S3,
  output S2,
  output S1,
  output S0,
  output Bout
);

  wire full_subtractor_1_2_bout, full_subtractor_1_3_bout, full_subtractor_1_4_bout;

  full_subtractor_1 full_subtractor_1_1 (.A(A3), .B(B3), .Bin(full_subtractor_1_2_bout), .D(S3), .Bout(Bout));
  full_subtractor_1 full_subtractor_1_2 (
    .A(A2), .B(B2), .Bin(full_subtractor_1_3_bout), .D(S2), .Bout(full_subtractor_1_2_bout));
  full_subtractor_1 full_subtractor_1_3 (
    .A(A1), .B(B1), .Bin(full_subtractor_1_4_bout), .D(S1), .Bout(full_subtractor_1_3_bout));
  full_subtractor_1 full_subtractor_1_4 (.A(A0), .B(B0), .Bin(Bin), .D(S0), .Bout(full_subtractor_1_4_bout));
endmodule

module half_subtractor_1 (
  input  A,
  input  B,
  output Y,
  output C
);

  wire not_1_out;

  not not_1 (not_1_out, A);
  xor xor_1 (Y, A, B);
  and and_1 (C, not_1_out, B);

  // Notes on the sheet:
  //   A-B=Y
endmodule

module full_subtractor_1 (
  input  A,
  input  B,
  input  Bin,
  output D,
  output Bout
);

  wire half_subtractor_1_1_c, half_subtractor_1_1_y, half_subtractor_1_2_c;

  half_subtractor_1 half_subtractor_1_1 (.A(A), .B(B), .Y(half_subtractor_1_1_y), .C(half_subtractor_1_1_c));
  half_subtractor_1 half_subtractor_1_2 (.A(half_subtractor_1_1_y), .B(Bin), .Y(D), .C(half_subtractor_1_2_c));
  or or_1 (Bout, half_subtractor_1_2_c, half_subtractor_1_1_c);
endmodule
